# Fritzing sketch Untitled Sketch 2 (saved by Fritzing 0.9.3b)
breadboards: 1

parts:
  Composant1 = Arduino Uno (Rev3) - ICSP
  J1 = Basic Servo
  LED1 = LED - 5mm [color="Red (633nm)" package="5 mm [THT]"]
  R1 = Photocell (LDR) [package=THT]
  R2 = Resistor [tolerance=±5% resistance=10k package="2010 [SMD]"]
  R3 = Resistor [tolerance=±5% resistance=330 package="2010 [SMD]"]
  S1 = Pushbutton [package="[THT]"]
  U1 = LCD-16X2 [package=lcd-16x2]  # not connected
  R4 = Resistor [tolerance=±5% resistance=10k package="2010 [SMD]"]

nets:
  N1: Composant1.A0, R1.pin_0, R2.Pin_1
  N2: Composant1.D9_PWM, J1.pulse
  GND: Composant1.GND, J1.gnd, R2.Pin_0, R3.Pin_0, S1.Pin_3, S1.Pin_4
  N3: Composant1.D2, LED1.anode
  N4: Composant1.D3_PWM, S1.Pin_1, S1.Pin_2, R4.Pin_1
  5V: Composant1.5V, J1.vcc, R1.pin_1, R4.Pin_0
  N5: LED1.cathode, R3.Pin_1
